# Fritzing sketch Final Circuit (saved by Fritzing 0.9.3b)
breadboards: 1

parts:
  Part1 = Arduino Uno (Rev3) - ICSP
  Part2 = RFID-RC522-v2
  J1 = Basic Servo
  LED4 = DUO LED RG [package="5 mm [THT]"]
  J2 = Piezo Speaker
  R1 = Resistor [tolerance=±5% resistance=220 package="0603 [SMD]"]
  R2 = Resistor [tolerance=±5% resistance=220 package="0603 [SMD]"]
  U1 = NodeMCU V1.0
  Part3 = LCD1602-I2C
  Water_Level_Sensor1 = Water Level Sensor
  FC-1 = Sound Sensor
  LED5 = smd LED [color="Red (633nm)" package="0805 [SMD]"]
  LED6 = smd LED [color="Red (633nm)" package="0805 [SMD]"]
  LED7 = smd LED [color="Red (633nm)" package="0805 [SMD]"]
  R3 = Resistor [tolerance=±5% resistance=220 package="0603 [SMD]"]
  R4 = Resistor [tolerance=±5% resistance=220 package="0603 [SMD]"]
  R5 = Resistor [tolerance=±5% resistance=220 package="0603 [SMD]"]
  R6 = Photocell (LDR) [package=THT]
  R7 = Resistor [tolerance=±5% resistance=220 package="0603 [SMD]"]
  RHT1 = Humidity and Temperature Sensor RHT03
  R8 = Resistor [tolerance=±5% resistance=220 package="0603 [SMD]"]
  R9 = Resistor [tolerance=±5% resistance=220 package="0603 [SMD]"]

nets:
  N1: Part1.A0, R6.pin_1, R7.Pin_0
  N2: Part1.A1, Water_Level_Sensor1.SIG
  N3: Part1.D8, R9.Pin_0
  N4: Part1.D9_PWM, Part2.RST
  N5: Part1.D10_PWM/SS, Part2.SDA
  N6: Part1.D11_PWM/MOSI, Part2.MOSI
  N7: Part1.D12/MISO, Part2.MISO
  N8: Part1.D13/SCK, Part2.SCK
  GND: Part1.GND, Part2.GND, J1.gnd, LED4.common_cathode, J2.pin1, U1.GND, Part3.GND, FC-1.GND, LED5.cathode, LED6.cathode, LED7.cathode, R7.Pin_1, RHT1.GND_1, RHT1.GND_2
  N9: Part1.D2, J2.pin2
  N10: Part1.D3_PWM, J1.pulse
  N11: Part1.D4, R1.Pin_0
  N12: Part1.D5_PWM, R2.Pin_0
  N13: Part1.D7, R8.Pin_0
  3V3: Part1.3V3, Part2.3.3V
  VCC: Part1.5V, J1.vcc, U1.Vin, Part3.VCC, FC-1.VCC, R6.pin_0, RHT1.Vcc
  N14: LED4.red_anode, R1.Pin_1
  N15: LED4.green_anode, R2.Pin_1
  N16: U1.D0, R8.Pin_1
  N17: U1.D1, Part3.SCL
  N18: U1.D2, Part3.SDA
  N19: U1.D3, RHT1.Data-signal
  N20: U1.D5, R3.Pin_1
  N21: U1.D6, R4.Pin_1
  N22: U1.D7, R5.Pin_1
  N23: U1.D8, R9.Pin_1
  N24: U1.A0, FC-1.OUT
  N25: LED5.anode, R3.Pin_0
  N26: LED6.anode, R4.Pin_0
  N27: LED7.anode, R5.Pin_0

custom parts:
  RFID-RC522-v2: A simple China made RFID-RC522 Reader; do check the pin labels, as this is a MFRC522 based clone.
  NodeMCU V1.0: ESP8266 based NodeMCU
  LCD1602-I2C: A standard character display, usually with 2x16 characters. Comes in many colors with LCM1602 IIC attached.
  Water Level Sensor: A water level sensor. This sensor operates at 3V to 5V. The Sig (signal) pin outputs an analogue signal that is in proportion to the amount of water in contact with the sensor.
