# Fritzing sketch Temperature and Humidity fritzing (saved by Fritzing 0.9.3b)
breadboards: 1

parts:
  RHT1 = Humidity and Temperature Sensor RHT03
  Adafruit_HUZZAH_ESP8266_Breakout1 = Adafruit HUZZAH ESP8266 Breakout [part_number=2471]

nets:
  N1: RHT1.Vcc, Adafruit_HUZZAH_ESP8266_Breakout1.#13
  N2: RHT1.Data-signal, Adafruit_HUZZAH_ESP8266_Breakout1.#4
  N3: RHT1.GND_2, Adafruit_HUZZAH_ESP8266_Breakout1.GND
